// Logisim project HW1-Part1.circ as structural Verilog: 2 circuits, main circuit 8-Bit Register
module _8_Bit_Register (
  input  [7:0] INPUT,
  input  ENABLE,
  input  [1:0] FUNSEL,
  output [7:0] OUTPUT__Q
);

  wire adder_1_cout, adder_1_out, adder_2_cout, adder_2_out, adder_3_cout, adder_3_out, adder_4_cout,
       adder_4_out, adder_5_cout, adder_5_out, adder_6_cout, adder_6_out, adder_7_cout, adder_7_out,
       adder_8_out, clock_1_out, multiplexer_1_out, multiplexer_2_out, multiplexer_3_out, multiplexer_4_out,
       multiplexer_5_out, multiplexer_6_out, multiplexer_7_out, multiplexer_8_out;

  Hex_Digit_Display hex_digit_display_1 (.value(INPUT[7:4]), .dp(1'b1));
  Hex_Digit_Display hex_digit_display_2 (.value(OUTPUT__Q[7:4]), .dp(1'b1));
  Hex_Digit_Display hex_digit_display_3 (.value(INPUT[3:0]), .dp(1'b1));
  Hex_Digit_Display hex_digit_display_4 (.value(OUTPUT__Q[3:0]), .dp(1'b1));
  Adder #(.width(1)) adder_1 (.a(OUTPUT__Q[0]), .b(1'b1), .out(adder_1_out), .cout(adder_1_cout));  // open: cin
  Adder #(.width(1)) adder_2 (
    .a(OUTPUT__Q[1]), .b(FUNSEL[0]), .out(adder_2_out), .cin(adder_1_cout), .cout(adder_2_cout));
  Adder #(.width(1)) adder_3 (
    .a(OUTPUT__Q[2]), .b(FUNSEL[0]), .out(adder_3_out), .cin(adder_2_cout), .cout(adder_3_cout));
  Adder #(.width(1)) adder_4 (
    .a(OUTPUT__Q[3]), .b(FUNSEL[0]), .out(adder_4_out), .cin(adder_3_cout), .cout(adder_4_cout));
  Adder #(.width(1)) adder_5 (
    .a(OUTPUT__Q[4]), .b(FUNSEL[0]), .out(adder_5_out), .cin(adder_4_cout), .cout(adder_5_cout));
  Adder #(.width(1)) adder_6 (
    .a(OUTPUT__Q[5]), .b(FUNSEL[0]), .out(adder_6_out), .cin(adder_5_cout), .cout(adder_6_cout));
  Adder #(.width(1)) adder_7 (
    .a(OUTPUT__Q[6]), .b(FUNSEL[0]), .out(adder_7_out), .cin(adder_6_cout), .cout(adder_7_cout));
  Adder #(.width(1)) adder_8 (.a(OUTPUT__Q[7]), .b(FUNSEL[0]), .out(adder_8_out), .cin(adder_7_cout));  // open: cout
  Clock clock_1 (.out(clock_1_out));
  Multiplexer #(.select(2), .enable("false")) multiplexer_1 (
    .in0(INPUT[0]), .in1(adder_1_out), .in2(adder_1_out), .in3(1'b0), .out(multiplexer_1_out), .sel(FUNSEL));
  Multiplexer #(.select(2), .enable("false")) multiplexer_2 (
    .in0(INPUT[1]), .in1(adder_2_out), .in2(adder_2_out), .in3(1'b0), .out(multiplexer_2_out), .sel(FUNSEL));
  Multiplexer #(.select(2), .enable("false")) multiplexer_3 (
    .in0(INPUT[2]), .in1(adder_3_out), .in2(adder_3_out), .in3(1'b0), .out(multiplexer_3_out), .sel(FUNSEL));
  Multiplexer #(.select(2), .enable("false")) multiplexer_4 (
    .in0(INPUT[3]), .in1(adder_4_out), .in2(adder_4_out), .in3(1'b0), .out(multiplexer_4_out), .sel(FUNSEL));
  Multiplexer #(.select(2), .enable("false")) multiplexer_5 (
    .in0(INPUT[4]), .in1(adder_5_out), .in2(adder_5_out), .in3(1'b0), .out(multiplexer_5_out), .sel(FUNSEL));
  Multiplexer #(.select(2), .enable("false")) multiplexer_6 (
    .in0(INPUT[5]), .in1(adder_6_out), .in2(adder_6_out), .in3(1'b0), .out(multiplexer_6_out), .sel(FUNSEL));
  Multiplexer #(.select(2), .enable("false")) multiplexer_7 (
    .in0(INPUT[6]), .in1(adder_7_out), .in2(adder_7_out), .in3(1'b0), .out(multiplexer_7_out), .sel(FUNSEL));
  Multiplexer #(.select(2), .enable("false")) multiplexer_8 (
    .in0(INPUT[7]), .in1(adder_8_out), .in2(adder_8_out), .in3(1'b0), .out(multiplexer_8_out), .sel(FUNSEL));
  D_Flip_Flop d_ff_1 (
    .clk(clock_1_out), .D(multiplexer_1_out), .Q(OUTPUT__Q[0]), .en(ENABLE));  // open: Qn, preset, reset
  D_Flip_Flop d_ff_2 (
    .clk(clock_1_out), .D(multiplexer_2_out), .Q(OUTPUT__Q[1]), .en(ENABLE));  // open: Qn, preset, reset
  D_Flip_Flop d_ff_3 (
    .clk(clock_1_out), .D(multiplexer_3_out), .Q(OUTPUT__Q[2]), .en(ENABLE));  // open: Qn, preset, reset
  D_Flip_Flop d_ff_4 (
    .clk(clock_1_out), .D(multiplexer_4_out), .Q(OUTPUT__Q[3]), .en(ENABLE));  // open: Qn, preset, reset
  D_Flip_Flop d_ff_5 (
    .clk(clock_1_out), .D(multiplexer_5_out), .Q(OUTPUT__Q[4]), .en(ENABLE));  // open: Qn, preset, reset
  D_Flip_Flop d_ff_6 (
    .clk(clock_1_out), .D(multiplexer_6_out), .Q(OUTPUT__Q[5]), .en(ENABLE));  // open: Qn, preset, reset
  D_Flip_Flop d_ff_7 (
    .clk(clock_1_out), .D(multiplexer_7_out), .Q(OUTPUT__Q[6]), .en(ENABLE));  // open: Qn, preset, reset
  D_Flip_Flop d_ff_8 (
    .clk(clock_1_out), .D(multiplexer_8_out), .Q(OUTPUT__Q[7]), .en(ENABLE));  // open: Qn, preset, reset

  // Notes on the sheet:
  //   INPUT
  //   Q OUTPUTS
endmodule

module _16_Bit_Register (
  input  [15:0] in_1,
  input  ENABLE,
  input  [1:0] FUNSEL,
  output [15:0] OUTPUT__Q
);

  wire adder_1_cout, adder_1_out, adder_2_cout, adder_2_out, adder_3_cout, adder_3_out, adder_4_cout,
       adder_4_out, adder_5_cout, adder_5_out, adder_6_cout, adder_6_out, adder_7_cout, adder_7_out,
       adder_8_cout, adder_8_out, adder_9_cout, adder_9_out, adder_10_cout, adder_10_out, adder_11_cout,
       adder_11_out, adder_12_cout, adder_12_out, adder_13_cout, adder_13_out, adder_14_cout, adder_14_out,
       adder_15_cout, adder_15_out, adder_16_out, clock_1_out, demultiplexer_1_out1, multiplexer_1_out,
       multiplexer_2_out, multiplexer_3_out, multiplexer_4_out, multiplexer_5_out, multiplexer_6_out,
       multiplexer_7_out, multiplexer_8_out, multiplexer_9_out, multiplexer_10_out, multiplexer_11_out,
       multiplexer_12_out, multiplexer_13_out, multiplexer_14_out, multiplexer_15_out, multiplexer_16_out;

  Hex_Digit_Display hex_digit_display_1 (.value(in_1[15:12]), .dp(1'b1));
  Hex_Digit_Display hex_digit_display_2 (.value(OUTPUT__Q[15:12]), .dp(1'b1));
  Hex_Digit_Display hex_digit_display_3 (.value(in_1[11:8]), .dp(1'b1));
  Hex_Digit_Display hex_digit_display_4 (.value(OUTPUT__Q[11:8]), .dp(1'b1));
  Hex_Digit_Display hex_digit_display_5 (.value(in_1[3:0]), .dp(1'b1));
  Hex_Digit_Display hex_digit_display_6 (.value(in_1[7:4]), .dp(1'b1));
  Hex_Digit_Display hex_digit_display_7 (.value(OUTPUT__Q[3:0]), .dp(1'b1));
  Hex_Digit_Display hex_digit_display_8 (.value(OUTPUT__Q[7:4]), .dp(1'b1));
  Demultiplexer #(.enable("false")) demultiplexer_1 (
    .out1(demultiplexer_1_out1), .in(1'b1), .sel(FUNSEL[0]));  // open: out0
  Adder #(.width(1)) adder_1 (.a(OUTPUT__Q[0]), .b(1'b1), .out(adder_1_out), .cout(adder_1_cout));  // open: cin
  Adder #(.width(1)) adder_2 (
    .a(OUTPUT__Q[1]), .b(demultiplexer_1_out1), .out(adder_2_out), .cin(adder_1_cout), .cout(adder_2_cout));
  Adder #(.width(1)) adder_3 (
    .a(OUTPUT__Q[2]), .b(demultiplexer_1_out1), .out(adder_3_out), .cin(adder_2_cout), .cout(adder_3_cout));
  Adder #(.width(1)) adder_4 (
    .a(OUTPUT__Q[3]), .b(demultiplexer_1_out1), .out(adder_4_out), .cin(adder_3_cout), .cout(adder_4_cout));
  Adder #(.width(1)) adder_5 (
    .a(OUTPUT__Q[4]), .b(demultiplexer_1_out1), .out(adder_5_out), .cin(adder_4_cout), .cout(adder_5_cout));
  Adder #(.width(1)) adder_6 (
    .a(OUTPUT__Q[5]), .b(demultiplexer_1_out1), .out(adder_6_out), .cin(adder_5_cout), .cout(adder_6_cout));
  Adder #(.width(1)) adder_7 (
    .a(OUTPUT__Q[6]), .b(demultiplexer_1_out1), .out(adder_7_out), .cin(adder_6_cout), .cout(adder_7_cout));
  Adder #(.width(1)) adder_8 (
    .a(OUTPUT__Q[7]), .b(demultiplexer_1_out1), .out(adder_8_out), .cin(adder_7_cout), .cout(adder_8_cout));
  Adder #(.width(1)) adder_9 (
    .a(OUTPUT__Q[8]), .b(demultiplexer_1_out1), .out(adder_9_out), .cin(adder_8_cout), .cout(adder_9_cout));
  Adder #(.width(1)) adder_10 (
    .a(OUTPUT__Q[9]), .b(demultiplexer_1_out1), .out(adder_10_out), .cin(adder_9_cout), .cout(adder_10_cout));
  Adder #(.width(1)) adder_11 (
    .a(OUTPUT__Q[10]), .b(demultiplexer_1_out1), .out(adder_11_out), .cin(adder_10_cout), .cout(adder_11_cout));
  Adder #(.width(1)) adder_12 (
    .a(OUTPUT__Q[11]), .b(demultiplexer_1_out1), .out(adder_12_out), .cin(adder_11_cout), .cout(adder_12_cout));
  Adder #(.width(1)) adder_13 (
    .a(OUTPUT__Q[12]), .b(demultiplexer_1_out1), .out(adder_13_out), .cin(adder_12_cout), .cout(adder_13_cout));
  Adder #(.width(1)) adder_14 (
    .a(OUTPUT__Q[13]), .b(demultiplexer_1_out1), .out(adder_14_out), .cin(adder_13_cout), .cout(adder_14_cout));
  Adder #(.width(1)) adder_15 (
    .a(OUTPUT__Q[14]), .b(demultiplexer_1_out1), .out(adder_15_out), .cin(adder_14_cout), .cout(adder_15_cout));
  Adder #(.width(1)) adder_16 (
    .a(OUTPUT__Q[15]), .b(demultiplexer_1_out1), .out(adder_16_out), .cin(adder_15_cout));  // open: cout
  Multiplexer #(.select(2), .enable("false")) multiplexer_1 (
    .in0(in_1[0]), .in1(adder_1_out), .in2(adder_1_out), .in3(1'b0), .out(multiplexer_1_out), .sel(FUNSEL));
  Multiplexer #(.select(2), .enable("false")) multiplexer_2 (
    .in0(in_1[1]), .in1(adder_2_out), .in2(adder_2_out), .in3(1'b0), .out(multiplexer_2_out), .sel(FUNSEL));
  Multiplexer #(.select(2), .enable("false")) multiplexer_3 (
    .in0(in_1[2]), .in1(adder_3_out), .in2(adder_3_out), .in3(1'b0), .out(multiplexer_3_out), .sel(FUNSEL));
  Multiplexer #(.select(2), .enable("false")) multiplexer_4 (
    .in0(in_1[3]), .in1(adder_4_out), .in2(adder_4_out), .in3(1'b0), .out(multiplexer_4_out), .sel(FUNSEL));
  Multiplexer #(.select(2), .enable("false")) multiplexer_5 (
    .in0(in_1[4]), .in1(adder_5_out), .in2(adder_5_out), .in3(1'b0), .out(multiplexer_5_out), .sel(FUNSEL));
  Multiplexer #(.select(2), .enable("false")) multiplexer_6 (
    .in0(in_1[5]), .in1(adder_6_out), .in2(adder_6_out), .in3(1'b0), .out(multiplexer_6_out), .sel(FUNSEL));
  Multiplexer #(.select(2), .enable("false")) multiplexer_7 (
    .in0(in_1[6]), .in1(adder_7_out), .in2(adder_7_out), .in3(1'b0), .out(multiplexer_7_out), .sel(FUNSEL));
  Multiplexer #(.select(2), .enable("false")) multiplexer_8 (
    .in0(in_1[7]), .in1(adder_8_out), .in2(adder_8_out), .in3(1'b0), .out(multiplexer_8_out), .sel(FUNSEL));
  Multiplexer #(.select(2), .enable("false")) multiplexer_9 (
    .in0(in_1[8]), .in1(adder_9_out), .in2(adder_9_out), .in3(1'b0), .out(multiplexer_9_out), .sel(FUNSEL));
  Multiplexer #(.select(2), .enable("false")) multiplexer_10 (
    .in0(in_1[9]), .in1(adder_10_out), .in2(adder_10_out), .in3(1'b0), .out(multiplexer_10_out), .sel(FUNSEL));
  Multiplexer #(.select(2), .enable("false")) multiplexer_11 (
    .in0(in_1[10]), .in1(adder_11_out), .in2(adder_11_out), .in3(1'b0), .out(multiplexer_11_out), .sel(FUNSEL));
  Multiplexer #(.select(2), .enable("false")) multiplexer_12 (
    .in0(in_1[11]), .in1(adder_12_out), .in2(adder_12_out), .in3(1'b0), .out(multiplexer_12_out), .sel(FUNSEL));
  Multiplexer #(.select(2), .enable("false")) multiplexer_13 (
    .in0(in_1[12]), .in1(adder_13_out), .in2(adder_13_out), .in3(1'b0), .out(multiplexer_13_out), .sel(FUNSEL));
  Multiplexer #(.select(2), .enable("false")) multiplexer_14 (
    .in0(in_1[13]), .in1(adder_14_out), .in2(adder_14_out), .in3(1'b0), .out(multiplexer_14_out), .sel(FUNSEL));
  Multiplexer #(.select(2), .enable("false")) multiplexer_15 (
    .in0(in_1[14]), .in1(adder_15_out), .in2(adder_15_out), .in3(1'b0), .out(multiplexer_15_out), .sel(FUNSEL));
  Multiplexer #(.select(2), .enable("false")) multiplexer_16 (
    .in0(in_1[15]), .in1(adder_16_out), .in2(adder_16_out), .in3(1'b0), .out(multiplexer_16_out), .sel(FUNSEL));
  Clock clock_1 (.out(clock_1_out));
  D_Flip_Flop d_ff_1 (
    .clk(clock_1_out), .D(multiplexer_1_out), .Q(OUTPUT__Q[0]), .en(ENABLE));  // open: Qn, preset, reset
  D_Flip_Flop d_ff_2 (
    .clk(clock_1_out), .D(multiplexer_2_out), .Q(OUTPUT__Q[1]), .en(ENABLE));  // open: Qn, preset, reset
  D_Flip_Flop d_ff_3 (
    .clk(clock_1_out), .D(multiplexer_3_out), .Q(OUTPUT__Q[2]), .en(ENABLE));  // open: Qn, preset, reset
  D_Flip_Flop d_ff_4 (
    .clk(clock_1_out), .D(multiplexer_4_out), .Q(OUTPUT__Q[3]), .en(ENABLE));  // open: Qn, preset, reset
  D_Flip_Flop d_ff_5 (
    .clk(clock_1_out), .D(multiplexer_5_out), .Q(OUTPUT__Q[4]), .en(ENABLE));  // open: Qn, preset, reset
  D_Flip_Flop d_ff_6 (
    .clk(clock_1_out), .D(multiplexer_6_out), .Q(OUTPUT__Q[5]), .en(ENABLE));  // open: Qn, preset, reset
  D_Flip_Flop d_ff_7 (
    .clk(clock_1_out), .D(multiplexer_7_out), .Q(OUTPUT__Q[6]), .en(ENABLE));  // open: Qn, preset, reset
  D_Flip_Flop d_ff_8 (
    .clk(clock_1_out), .D(multiplexer_8_out), .Q(OUTPUT__Q[7]), .en(ENABLE));  // open: Qn, preset, reset
  D_Flip_Flop d_ff_9 (
    .clk(clock_1_out), .D(multiplexer_9_out), .Q(OUTPUT__Q[8]), .en(ENABLE));  // open: Qn, preset, reset
  D_Flip_Flop d_ff_10 (
    .clk(clock_1_out), .D(multiplexer_10_out), .Q(OUTPUT__Q[9]), .en(ENABLE));  // open: Qn, preset, reset
  D_Flip_Flop d_ff_11 (
    .clk(clock_1_out), .D(multiplexer_11_out), .Q(OUTPUT__Q[10]), .en(ENABLE));  // open: Qn, preset, reset
  D_Flip_Flop d_ff_12 (
    .clk(clock_1_out), .D(multiplexer_12_out), .Q(OUTPUT__Q[11]), .en(ENABLE));  // open: Qn, preset, reset
  D_Flip_Flop d_ff_13 (
    .clk(clock_1_out), .D(multiplexer_13_out), .Q(OUTPUT__Q[12]), .en(ENABLE));  // open: Qn, preset, reset
  D_Flip_Flop d_ff_14 (
    .clk(clock_1_out), .D(multiplexer_14_out), .Q(OUTPUT__Q[13]), .en(ENABLE));  // open: Qn, preset, reset
  D_Flip_Flop d_ff_15 (
    .clk(clock_1_out), .D(multiplexer_15_out), .Q(OUTPUT__Q[14]), .en(ENABLE));  // open: Qn, preset, reset
  D_Flip_Flop d_ff_16 (
    .clk(clock_1_out), .D(multiplexer_16_out), .Q(OUTPUT__Q[15]), .en(ENABLE));  // open: Qn, preset, reset

  // Notes on the sheet:
  //   INPUT
  //   Q OUTPUTS
endmodule
