// Logisim project HW2-Part1.circ as structural Verilog: 1 circuit, main circuit ALU
module ALU (
  input  [7:0] A,
  input  [7:0] B,
  input  Cin,
  input  [3:0] FunSel,
  output [7:0] OutALU,
  output [3:0] OutFlag_ZCNO
);

  wire adder_1_cout, adder_2_cout, and_2_out, and_3_out, and_4_out, and_5_out, or_2_out, or_3_out,
       subtractor_1_bout, xor_2_out, xor_3_out;
  wire [7:0] A_B, A_B_Carry, A_B_t, AandB, AorB, AxorB, not_1_out, not_2_out, shifter_1_out, shifter_2_out,
       shifter_3_out, shifter_4_out, shifter_5_out, shifter_6_out;

  Adder adder_1 (.a(A), .b(B), .out(A_B), .cout(adder_1_cout));  // open: cin
  Adder adder_2 (.a(B), .b(A), .out(A_B_Carry), .cin(Cin), .cout(adder_2_cout));
  Subtractor subtractor_1 (.a(A), .b(B), .out(A_B_t), .bout(subtractor_1_bout));  // open: bin
  assign AandB = A & B;  // AND_Gate and_1, 8 bits wide
  assign AorB = A | B;  // OR_Gate or_1, 8 bits wide
  assign AxorB = A ^ B;  // XOR_Gate xor_1, 8 bits wide
  Shifter shifter_1 (.in(A), .\dist (3'b001), .out(shifter_1_out));
  Shifter #(.shift("lr")) shifter_2 (.in(A), .\dist (3'b001), .out(shifter_2_out));
  Shifter shifter_3 (.in(A), .\dist (3'b001), .out(shifter_3_out));
  Shifter #(.shift("ar")) shifter_4 (.in(A), .\dist (3'b001), .out(shifter_4_out));
  Shifter #(.shift("rl")) shifter_5 (.in(A), .\dist (3'b001), .out(shifter_5_out));
  Shifter #(.shift("rr")) shifter_6 (.in(A), .\dist (3'b001), .out(shifter_6_out));
  assign not_1_out = ~B;  // NOT_Gate not_1, 8 bits wide
  Multiplexer #(.select(4), .enable("false")) multiplexer_1 (
    .in5(adder_1_cout), .in6(adder_2_cout), .in7(subtractor_1_bout), .in10(A[7]), .in11(A[0]), .in14(A[7]),
    .in15(A[0]), .out(OutFlag_ZCNO[2]), .sel(FunSel));  // open: in0, in1, in2, in3, in4, in8, in9, in12, in13
  assign not_2_out = ~A;  // NOT_Gate not_2, 8 bits wide
  xor xor_2 (xor_2_out, A[6], A[7]);
  xor xor_3 (xor_3_out, A[7], A[0]);
  Hex_Digit_Display hex_digit_display_1 (.value(OutALU[7:4]));  // open: dp
  Multiplexer #(.select(4), .width(8), .enable("false")) multiplexer_2 (
    .in0(AandB), .in1(AorB), .in2(not_2_out), .in3(AxorB), .in4(A), .in5(A_B), .in6(A_B_Carry), .in7(A_B_t),
    .in8(B), .in9(not_1_out), .in10(shifter_1_out), .in11(shifter_2_out), .in12(shifter_3_out),
    .in13(shifter_4_out), .in14(shifter_5_out), .in15(shifter_6_out), .out(OutALU), .sel(FunSel));
  and and_2 (and_2_out, ~A[7], ~B[7], OutALU[7]);  // AND_Gate
  or or_2 (or_2_out, and_2_out, and_3_out);
  and and_3 (and_3_out, A[7], B[7], ~OutALU[7]);  // AND_Gate
  and and_4 (and_4_out, ~A[7], B[7], OutALU[7]);  // AND_Gate
  or or_3 (or_3_out, and_4_out, and_5_out);
  and and_5 (and_5_out, A[7], ~B[7], ~OutALU[7]);  // AND_Gate
  Hex_Digit_Display hex_digit_display_2 (.value(OutALU[3:0]));  // open: dp
  Multiplexer #(.select(4), .enable("false")) multiplexer_3 (
    .in5(or_2_out), .in6(or_2_out), .in7(or_3_out), .in12(xor_2_out), .in14(xor_2_out), .in15(xor_3_out),
    .out(OutFlag_ZCNO[0]), .sel(FunSel));  // open: in0, in1, in2, in3, in4, in8, in9, in10, in11, in13
  Comparator comparator_1 (.a(OutALU), .b({8{1'b0}}), .eq(OutFlag_ZCNO[3]), .lt(OutFlag_ZCNO[1]));  // open: gt

  // Other names for the same wires on the sheet: MSB_B = B[7]; MSB_OUT = OutALU[7]; O = OutFlag_ZCNO[0];
  //   C = OutFlag_ZCNO[2]

  // Notes on the sheet:
  //   LSL
  //   LSR
  //   ASL
  //   ASR
  //   CSL
  //   CSR
  //   Shift Overflow
  //   Addition Overflow
  //   Subtraction Overflow
endmodule
