// Logisim project HW2-Part2.circ as structural Verilog: 1 circuit, main circuit Organization
// Address Register File
module Organization (
  input  [1:0] OutASel,
  input  [3:0] FunSel,
  input  [1:0] OutBSel,
  input  [1:0] FunSel_2,
  input  [3:0] RegSel,
  input  [1:0] in_6,
  input  [1:0] in_7,
  input  [1:0] OutCSel,
  input  in_9,
  input  in_10,
  input  [1:0] FunSel_3,
  input  [2:0] RegSel_2,
  input  L_H_prime,
  input  Enable,
  input  [1:0] FunSel_4,
  output [7:0] IR__8_15
);

  wire button_1_out, clock_1_out;
  wire [3:0] alu_1_outflag_zcno;
  wire [7:0] a_general_purpose_1_outa, a_general_purpose_1_outb, alu_1_outalu, b_pc_ar_sp_1_out_5,
       c_ir_1_out_5, multiplexer_1_out, multiplexer_2_out, ram_1_data;

  Multiplexer #(.select(2), .width(8), .enable("false")) multiplexer_1 (
    .in0(c_ir_1_out_5), .in1(ram_1_data), .in2(b_pc_ar_sp_1_out_5), .in3(alu_1_outalu),
    .out(multiplexer_1_out), .sel(in_6));
  A_General_Purpose a_general_purpose_1 (
    .I(multiplexer_1_out), .OutASel(OutASel), .OutBSel(OutBSel), .OutA(a_general_purpose_1_outa),
    .OutB(a_general_purpose_1_outb), .RegSel(RegSel), .FunSel(FunSel_2));
  C_IR c_ir_1 (.out_5({IR__8_15, c_ir_1_out_5}), .L_H_prime(L_H_prime), .I(ram_1_data), .E(Enable), .FunSel(FunSel_4));
  LED Z (.in(alu_1_outflag_zcno[3]));
  LED O (.in(alu_1_outflag_zcno[0]));
  LED C (.in(alu_1_outflag_zcno[2]));
  LED N (.in(alu_1_outflag_zcno[1]));
  ALU alu_1 (
    .FunSel(FunSel), .A(a_general_purpose_1_outa), .B(a_general_purpose_1_outb), .Cin(alu_1_outflag_zcno[2]),
    .OutALU(alu_1_outalu), .OutFlag_ZCNO(alu_1_outflag_zcno));
  Multiplexer #(.select(2), .width(8), .enable("false")) multiplexer_2 (
    .in1(c_ir_1_out_5), .in2(ram_1_data), .in3(alu_1_outalu), .out(multiplexer_2_out), .sel(in_7));  // open: in0
  B_PC_AR_SP b_pc_ar_sp_1 (
    .I(multiplexer_2_out), .FunSel(FunSel_3), .RegSel(RegSel_2), .OutCSel(OutCSel), .out_5(b_pc_ar_sp_1_out_5));
  Clock clock_1 (.out(clock_1_out));
  RAM #(.bus("separate")) ram_1 (
    .addr(b_pc_ar_sp_1_out_5), .din(alu_1_outalu), .data(ram_1_data), .str(in_9), .clk(clock_1_out),
    .ld(in_10), .clr(button_1_out));  // open: sel
  Button button_1 (.out(button_1_out));
endmodule
