// Logisim project HW1-Part2.circ as structural Verilog: 3 circuits, main circuit A-General Purpose
module A_General_Purpose (
  input  [7:0] I,
  input  [3:0] RegSel,
  input  [1:0] FunSel,
  input  [1:0] OutASel,
  input  [1:0] OutBSel,
  output [7:0] OutA,
  output [7:0] OutB
);

  wire [3:0] _0, _1, _2, _3, _4, _5, _6, _7;

  _8_Bit_Register u_8_bit_register_1 (
    .OUTPUT__Q({_7[0], _6[0], _5[0], _4[0], _3[0], _2[0], _1[0], _0[0]}), .FUNSEL(FunSel), .INPUT(I),
    .ENABLE(RegSel[3]));
  _8_Bit_Register u_8_bit_register_2 (
    .OUTPUT__Q({_7[1], _6[1], _5[1], _4[1], _3[1], _2[1], _1[1], _0[1]}), .FUNSEL(FunSel), .INPUT(I),
    .ENABLE(RegSel[2]));
  _8_Bit_Register u_8_bit_register_3 (
    .OUTPUT__Q({_7[2], _6[2], _5[2], _4[2], _3[2], _2[2], _1[2], _0[2]}), .FUNSEL(FunSel), .INPUT(I),
    .ENABLE(RegSel[1]));
  _8_Bit_Register u_8_bit_register_4 (
    .OUTPUT__Q({_7[3], _6[3], _5[3], _4[3], _3[3], _2[3], _1[3], _0[3]}), .FUNSEL(FunSel), .INPUT(I),
    .ENABLE(RegSel[0]));
  Multiplexer #(.select(2), .enable("false")) multiplexer_1 (
    .in0(_0[0]), .in1(_0[1]), .in2(_0[2]), .in3(_0[3]), .out(OutA[0]), .sel(OutASel));
  Multiplexer #(.select(2), .enable("false")) multiplexer_2 (
    .in0(_1[0]), .in1(_1[1]), .in2(_1[2]), .in3(_1[3]), .out(OutA[1]), .sel(OutASel));
  Multiplexer #(.select(2), .enable("false")) multiplexer_3 (
    .in0(_2[0]), .in1(_2[1]), .in2(_2[2]), .in3(_2[3]), .out(OutA[2]), .sel(OutASel));
  Multiplexer #(.select(2), .enable("false")) multiplexer_4 (
    .in0(_3[0]), .in1(_3[1]), .in2(_3[2]), .in3(_3[3]), .out(OutA[3]), .sel(OutASel));
  Multiplexer #(.select(2), .enable("false")) multiplexer_5 (
    .in0(_4[0]), .in1(_4[1]), .in2(_4[2]), .in3(_4[3]), .out(OutA[4]), .sel(OutASel));
  Multiplexer #(.select(2), .enable("false")) multiplexer_6 (
    .in0(_5[0]), .in1(_5[1]), .in2(_5[2]), .in3(_5[3]), .out(OutA[5]), .sel(OutASel));
  Multiplexer #(.select(2), .enable("false")) multiplexer_7 (
    .in0(_6[0]), .in1(_6[1]), .in2(_6[2]), .in3(_6[3]), .out(OutA[6]), .sel(OutASel));
  Multiplexer #(.select(2), .enable("false")) multiplexer_8 (
    .in0(_7[0]), .in1(_7[1]), .in2(_7[2]), .in3(_7[3]), .out(OutA[7]), .sel(OutASel));
  Hex_Digit_Display hex_digit_display_1 (.value(OutA[7:4]), .dp(1'b1));
  Hex_Digit_Display hex_digit_display_2 (.value(OutA[3:0]), .dp(1'b1));
  Multiplexer #(.select(2), .enable("false")) multiplexer_9 (
    .in0(_0[0]), .in1(_0[1]), .in2(_0[2]), .in3(_0[3]), .out(OutB[0]), .sel(OutBSel));
  Multiplexer #(.select(2), .enable("false")) multiplexer_10 (
    .in0(_1[0]), .in1(_1[1]), .in2(_1[2]), .in3(_1[3]), .out(OutB[1]), .sel(OutBSel));
  Multiplexer #(.select(2), .enable("false")) multiplexer_11 (
    .in0(_2[0]), .in1(_2[1]), .in2(_2[2]), .in3(_2[3]), .out(OutB[2]), .sel(OutBSel));
  Multiplexer #(.select(2), .enable("false")) multiplexer_12 (
    .in0(_3[0]), .in1(_3[1]), .in2(_3[2]), .in3(_3[3]), .out(OutB[3]), .sel(OutBSel));
  Multiplexer #(.select(2), .enable("false")) multiplexer_13 (
    .in0(_4[0]), .in1(_4[1]), .in2(_4[2]), .in3(_4[3]), .out(OutB[4]), .sel(OutBSel));
  Multiplexer #(.select(2), .enable("false")) multiplexer_14 (
    .in0(_5[0]), .in1(_5[1]), .in2(_5[2]), .in3(_5[3]), .out(OutB[5]), .sel(OutBSel));
  Multiplexer #(.select(2), .enable("false")) multiplexer_15 (
    .in0(_6[0]), .in1(_6[1]), .in2(_6[2]), .in3(_6[3]), .out(OutB[6]), .sel(OutBSel));
  Multiplexer #(.select(2), .enable("false")) multiplexer_16 (
    .in0(_7[0]), .in1(_7[1]), .in2(_7[2]), .in3(_7[3]), .out(OutB[7]), .sel(OutBSel));
  Hex_Digit_Display hex_digit_display_3 (.value(OutB[3:0]), .dp(1'b1));
  Hex_Digit_Display hex_digit_display_4 (.value(OutB[7:4]), .dp(1'b1));
endmodule

module B_PC_AR_SP (
  input  [1:0] OutDSel,
  input  [7:0] I,
  input  [2:0] RegSel,
  input  [1:0] FunSel,
  input  [1:0] OutCSel,
  output [7:0] OutD,
  output [7:0] OutC
);

  wire [7:0] AR_output__q, OutAR, OutPC, OutSP, PC_output__q, SP_output__q;

  _8_Bit_Register AR (.OUTPUT__Q(AR_output__q), .FUNSEL(FunSel), .INPUT(I), .ENABLE(RegSel[2]));
  _8_Bit_Register SP (.OUTPUT__Q(SP_output__q), .FUNSEL(FunSel), .INPUT(I), .ENABLE(RegSel[1]));
  _8_Bit_Register PC (.OUTPUT__Q(PC_output__q), .FUNSEL(FunSel), .INPUT(I), .ENABLE(RegSel[0]));
  Multiplexer #(.select(2), .enable("false")) multiplexer_1 (
    .in0(AR_output__q[0]), .in1(SP_output__q[0]), .in2(PC_output__q[0]), .in3(PC_output__q[0]),
    .out(OutC[0]), .sel(OutCSel));
  Multiplexer #(.select(2), .enable("false")) multiplexer_2 (
    .in0(AR_output__q[1]), .in1(SP_output__q[1]), .in2(PC_output__q[1]), .in3(PC_output__q[1]),
    .out(OutC[1]), .sel(OutCSel));
  Multiplexer #(.select(2), .enable("false")) multiplexer_3 (
    .in0(AR_output__q[2]), .in1(SP_output__q[2]), .in2(PC_output__q[2]), .in3(PC_output__q[2]),
    .out(OutC[2]), .sel(OutCSel));
  Multiplexer #(.select(2), .enable("false")) multiplexer_4 (
    .in0(AR_output__q[3]), .in1(SP_output__q[3]), .in2(PC_output__q[3]), .in3(PC_output__q[3]),
    .out(OutC[3]), .sel(OutCSel));
  Multiplexer #(.select(2), .enable("false")) multiplexer_5 (
    .in0(AR_output__q[4]), .in1(SP_output__q[4]), .in2(PC_output__q[4]), .in3(PC_output__q[4]),
    .out(OutC[4]), .sel(OutCSel));
  Multiplexer #(.select(2), .enable("false")) multiplexer_6 (
    .in0(AR_output__q[5]), .in1(SP_output__q[5]), .in2(PC_output__q[5]), .in3(PC_output__q[5]),
    .out(OutC[5]), .sel(OutCSel));
  Multiplexer #(.select(2), .enable("false")) multiplexer_7 (
    .in0(AR_output__q[6]), .in1(SP_output__q[6]), .in2(PC_output__q[6]), .in3(PC_output__q[6]),
    .out(OutC[6]), .sel(OutCSel));
  Multiplexer #(.select(2), .enable("false")) multiplexer_8 (
    .in0(AR_output__q[7]), .in1(SP_output__q[7]), .in2(PC_output__q[7]), .in3(PC_output__q[7]),
    .out(OutC[7]), .sel(OutCSel));
  Hex_Digit_Display hex_digit_display_1 (.value(OutC[7:4]));  // open: dp
  Hex_Digit_Display hex_digit_display_2 (.value(OutC[3:0]));  // open: dp
  Multiplexer #(.select(2), .width(8), .enable("false")) multiplexer_9 (
    .in0(OutAR), .in1(OutSP), .in2(OutPC), .in3(OutPC), .out(OutD), .sel(OutDSel));
endmodule

module C_IR (
  input  [1:0] FunSel,
  input  L_H_prime,
  input  E,
  input  [7:0] I,
  output [15:0] out_5
);

  wire [15:0] multiplexer_1_out;

  _16_Bit_Register u_16_bit_register_1 (.ENABLE(E), .OUTPUT__Q(out_5), .FUNSEL(FunSel), .in_1(multiplexer_1_out));
  Multiplexer #(.enable("false")) multiplexer_1 (
    .in0(I[0]), .in1(out_5[0]), .out(multiplexer_1_out[0]), .sel(L_H_prime));
  Multiplexer #(.enable("false")) multiplexer_2 (
    .in0(I[1]), .in1(out_5[1]), .out(multiplexer_1_out[1]), .sel(L_H_prime));
  Multiplexer #(.enable("false")) multiplexer_3 (
    .in0(I[2]), .in1(out_5[2]), .out(multiplexer_1_out[2]), .sel(L_H_prime));
  Multiplexer #(.enable("false")) multiplexer_4 (
    .in0(I[3]), .in1(out_5[3]), .out(multiplexer_1_out[3]), .sel(L_H_prime));
  Multiplexer #(.enable("false")) multiplexer_5 (
    .in0(I[4]), .in1(out_5[4]), .out(multiplexer_1_out[4]), .sel(L_H_prime));
  Multiplexer #(.enable("false")) multiplexer_6 (
    .in0(I[5]), .in1(out_5[5]), .out(multiplexer_1_out[5]), .sel(L_H_prime));
  Multiplexer #(.enable("false")) multiplexer_7 (
    .in0(I[6]), .in1(out_5[6]), .out(multiplexer_1_out[6]), .sel(L_H_prime));
  Multiplexer #(.enable("false")) multiplexer_8 (
    .in0(I[7]), .in1(out_5[7]), .out(multiplexer_1_out[7]), .sel(L_H_prime));
  Multiplexer #(.enable("false")) multiplexer_9 (
    .in0(out_5[8]), .in1(I[0]), .out(multiplexer_1_out[8]), .sel(L_H_prime));
  Multiplexer #(.enable("false")) multiplexer_10 (
    .in0(out_5[9]), .in1(I[1]), .out(multiplexer_1_out[9]), .sel(L_H_prime));
  Multiplexer #(.enable("false")) multiplexer_11 (
    .in0(out_5[10]), .in1(I[2]), .out(multiplexer_1_out[10]), .sel(L_H_prime));
  Multiplexer #(.enable("false")) multiplexer_12 (
    .in0(out_5[11]), .in1(I[3]), .out(multiplexer_1_out[11]), .sel(L_H_prime));
  Multiplexer #(.enable("false")) multiplexer_13 (
    .in0(out_5[12]), .in1(I[4]), .out(multiplexer_1_out[12]), .sel(L_H_prime));
  Multiplexer #(.enable("false")) multiplexer_14 (
    .in0(out_5[13]), .in1(I[5]), .out(multiplexer_1_out[13]), .sel(L_H_prime));
  Multiplexer #(.enable("false")) multiplexer_15 (
    .in0(out_5[14]), .in1(I[6]), .out(multiplexer_1_out[14]), .sel(L_H_prime));
  Multiplexer #(.enable("false")) multiplexer_16 (
    .in0(out_5[15]), .in1(I[7]), .out(multiplexer_1_out[15]), .sel(L_H_prime));
  Hex_Digit_Display hex_digit_display_1 (.value(out_5[11:8]));  // open: dp
  Hex_Digit_Display hex_digit_display_2 (.value(out_5[15:12]));  // open: dp
  Hex_Digit_Display hex_digit_display_3 (.value(out_5[7:4]));  // open: dp
  Hex_Digit_Display hex_digit_display_4 (.value(out_5[3:0]));  // open: dp
endmodule
