// Logisim project HW3.circ as structural Verilog: 2 circuits, main circuit main
module main (
  output O,
  output N,
  output C,
  output Z
);

  wire ASelALU, BSelALU, button_1_out, CFlagALU, Clock, EnableIR_prime, L_H_prime, NFlagALU, OFlagALU, Read,
       Write, ZFlagALU;
  wire [1:0] FunSelASP, FunSelGP, FunSelIR, OutASel, OutBSel, OutCSel, OutDSel, SelASP, SelGP;
  wire [2:0] RegSelASP;
  wire [3:0] FunSelALU, RegSelGP;
  wire [7:0] ALU_outalu, ASP_outc, ASP_outd, GPR_outa, GPR_outb, multiplexer_1_out, multiplexer_2_out,
       multiplexer_3_out, multiplexer_4_out, ram_1_data;
  wire [15:0] Instruction;

  Control_Unit control_unit_1 (
    .OutputRegSelASP(RegSelASP), .OutputBSelALU(BSelALU), .MEMRead(Read), .OutputSelGP(SelGP),
    .MEMWrite(Write), .OutputFunSelALU(FunSelALU), .OutASelALU(ASelALU), .OutputOutBSel(OutBSel),
    .OutputOutASel(OutASel), .OutputRegSelGP(RegSelGP), .OutputOutDSel(OutDSel), .OutputFunSelGP(FunSelGP),
    .OutputFunSelASP(FunSelASP), .OutputOutCsel(OutCSel), .Instruction(Instruction),
    .OutputFunSelIR(FunSelIR), .OutputEnableIR(EnableIR_prime), .OutputL_H(L_H_prime), .Z(Z),
    .OutputSelASP(SelASP));
  Multiplexer #(.select(2), .width(8), .enable("false")) multiplexer_1 (
    .in0(Instruction[7:0]), .in1(ram_1_data), .in2(ASP_outc), .in3(ALU_outalu), .out(multiplexer_1_out),
    .sel(SelGP));
  A_General_Purpose GPR (
    .I(multiplexer_1_out), .OutASel(OutASel), .OutBSel(OutBSel), .OutA(GPR_outa), .OutB(GPR_outb),
    .RegSel(RegSelGP), .FunSel(FunSelGP));
  C_IR c_ir_1 (.out_5(Instruction), .L_H_prime(L_H_prime), .I(ram_1_data), .E(EnableIR_prime), .FunSel(FunSelIR));
  Multiplexer #(.width(8), .enable("false")) multiplexer_2 (
    .in0(GPR_outa), .in1(ASP_outc), .out(multiplexer_2_out), .sel(ASelALU));
  Multiplexer #(.width(8), .enable("false")) multiplexer_3 (
    .in0(GPR_outb), .in1(ASP_outd), .out(multiplexer_3_out), .sel(BSelALU));
  Multiplexer #(.select(2), .width(8), .enable("false")) multiplexer_4 (
    .in0(ASP_outc), .in1(Instruction[7:0]), .in2(ram_1_data), .in3(ALU_outalu), .out(multiplexer_4_out),
    .sel(SelASP));
  ALU ALU (
    .FunSel(FunSelALU), .A(multiplexer_2_out), .B(multiplexer_3_out), .Cin(CFlagALU), .OutALU(ALU_outalu),
    .OutFlag_ZCNO({ZFlagALU, CFlagALU, NFlagALU, OFlagALU}));
  Clock clock_1 (.out(Clock));
  B_PC_AR_SP ASP (
    .I(multiplexer_4_out), .FunSel(FunSelASP), .RegSel(RegSelASP), .OutCSel(OutCSel), .OutC(ASP_outc),
    .OutD(ASP_outd), .OutDSel(OutDSel));
  D_Flip_Flop u_O (.clk(Clock), .D(OFlagALU), .Q(O), .en(1'b1));  // open: Qn, preset, reset
  D_Flip_Flop u_N (.clk(Clock), .D(NFlagALU), .Q(N), .en(1'b1));  // open: Qn, preset, reset
  D_Flip_Flop u_C (.clk(Clock), .D(CFlagALU), .Q(C), .en(1'b1));  // open: Qn, preset, reset
  D_Flip_Flop u_Z (.clk(Clock), .D(ZFlagALU), .Q(Z), .en(1'b1));  // open: Qn, preset, reset
  RAM #(.bus("separate")) ram_1 (
    .addr(ASP_outc), .din(ALU_outalu), .data(ram_1_data), .str(Write), .clk(Clock), .ld(Read),
    .clr(button_1_out));  // open: sel
  Button button_1 (.out(button_1_out));
endmodule

module Control_Unit (
  input  [15:0] Instruction,
  input  Z,
  output [1:0] OutputFunSelIR,
  output [1:0] OutputSelGP,
  output [1:0] OutputSelASP,
  output OutputEnableIR,
  output [3:0] OutputRegSelGP,
  output [2:0] OutputRegSelASP,
  output [1:0] OutputOutASel,
  output OutputL_H,
  output [1:0] OutputFunSelGP,
  output [1:0] OutputFunSelASP,
  output [1:0] OutputOutBSel,
  output MEMWrite,
  output [1:0] OutputOutCsel,
  output OutASelALU,
  output MEMRead,
  output [1:0] OutputOutDSel,
  output OutputBSelALU,
  output [3:0] OutputFunSelALU
);

  wire and_1_out, and_2_out, and_3_out, and_4_out, and_5_out, and_6_out, and_7_out, and_8_out, and_9_out,
       and_10_out, and_12_out, and_13_out, and_14_out, and_15_out, and_16_out, and_17_out, and_18_out,
       and_19_out, and_20_out, and_21_out, and_22_out, and_23_out, and_24_out, and_25_out, and_26_out,
       and_27_out, and_28_out, and_29_out, and_30_out, and_31_out, and_32_out, and_33_out, and_34_out,
       and_35_out, and_36_out, and_37_out, and_38_out, and_39_out, and_40_out, and_41_out, and_42_out,
       and_43_out, and_44_out, and_45_out, and_46_out, and_47_out, and_48_out, and_49_out, and_50_out,
       and_51_out, and_52_out, and_53_out, and_54_out, and_55_out, and_56_out, and_57_out, and_58_out,
       and_59_out, Clock, D0, D1, D2, D3, D4, D5, D6, D7, D8, D9, D10, D11, D12, D13, D14, d_ff_1_q,
       decoder_2_out2, decoder_2_out3, not_1_out, or_1_out, or_2_out, or_5_out, or_6_out, or_7_out, or_8_out,
       or_9_out, or_10_out, or_13_out, or_14_out, or_15_out, or_16_out, or_17_out, or_18_out, or_19_out,
       or_20_out, or_21_out, or_22_out, or_23_out, or_24_out, or_25_out, or_26_out, or_27_out, or_28_out,
       or_29_out, or_30_out, or_32_out, or_33_out, or_34_out, or_35_out, or_36_out, or_37_out, or_38_out,
       or_39_out, SC, T0, T1, T2, T3, T4, T5, T6, T7;
  wire [2:0] counter_1_q, RegSelASP_9_8;
  wire [3:0] RegSelGP_9_8, RegSelGP_10_9;

  Counter #(.width(3), .max('h7)) counter_1 (
    .count(1'b1), .Q(counter_1_q), .clk(Clock), .clr(d_ff_1_q));  // open: load, D, carry
  Clock clock_1 (.out(Clock));
  Decoder #(.select(3), .enable("false")) decoder_1 (
    .out0(T0), .out1(T1), .out2(T2), .out3(T3), .out4(T4), .out5(T5), .out6(T6), .out7(T7), .sel(counter_1_q));
  and and_1 (and_1_out, D9, T4, ~Instruction[8]);  // AND_Gate
  Decoder #(.select(2), .enable("false")) decoder_2 (
    .out0(RegSelASP_9_8[2]), .out1(RegSelASP_9_8[1]), .out2(decoder_2_out2), .out3(decoder_2_out3),
    .sel(Instruction[9:8]));
  and and_2 (and_2_out, T4, D10);
  or or_1 (or_1_out, D2, D3, D11);
  and and_3 (and_3_out, or_1_out, ~Instruction[7]);  // AND_Gate
  or or_2 (or_2_out, D0, D1, D7, D8, and_3_out, D12, D13, D14);
  D_Flip_Flop d_ff_1 (.clk(Clock), .D(SC), .Q(d_ff_1_q), .en(1'b1), .reset(d_ff_1_q));  // open: Qn, preset
  or or_3 (MEMRead, T0, and_1_out, T2);
  or or_4 (RegSelASP_9_8[0], decoder_2_out2, decoder_2_out3);
  and and_4 (and_4_out, Z, T4, D5);
  and and_5 (and_5_out, T4, D4);
  and and_6 (and_6_out, ~Z, T4, D6);  // AND_Gate
  and and_7 (and_7_out, D9, T4, Instruction[8]);
  and and_8 (and_8_out, D9, T4, ~Instruction[8]);  // AND_Gate
  and and_9 (and_9_out, or_1_out, ~Instruction[10], Instruction[7], T4);  // AND_Gate
  and and_10 (and_10_out, or_2_out, ~Instruction[10], T4);  // AND_Gate
  or or_5 (or_5_out, T1, T3, and_6_out, and_4_out, and_5_out);
  assign OutputRegSelASP = and_2_out ? 3'b100 : 3'bz;  // Controlled_Buffer controlled_buffer_1
  assign OutputSelGP = and_7_out ? 2'b00 : 2'bz;  // Controlled_Buffer controlled_buffer_2
  assign OutputSelGP = and_8_out ? 2'b01 : 2'bz;  // Controlled_Buffer controlled_buffer_3
  assign OutputSelGP = and_9_out ? 2'b10 : 2'bz;  // Controlled_Buffer controlled_buffer_4
  assign OutputSelGP = and_10_out ? 2'b11 : 2'bz;  // Controlled_Buffer controlled_buffer_5
  Decoder #(.select(2), .enable("false")) decoder_3 (
    .out0(RegSelGP_9_8[3]), .out1(RegSelGP_9_8[2]), .out2(RegSelGP_9_8[1]), .out3(RegSelGP_9_8[0]),
    .sel(Instruction[9:8]));
  assign OutputRegSelASP = or_5_out ? 3'b001 : 3'bz;  // Controlled_Buffer controlled_buffer_6
  and and_11 (MEMWrite, T4, D10);
  or or_6 (or_6_out, D0, D1, D2, D3, D7, D8, D11, D12, D13, D14);
  and and_12 (and_12_out, T4, or_6_out);
  or or_7 (or_7_out, D2, D3, D10, D11);
  or or_8 (or_8_out, D10, ~Instruction[7]);  // OR_Gate
  or or_9 (or_9_out, D2, D3);
  and and_13 (and_13_out, T5, or_9_out);
  or or_10 (or_10_out, and_12_out, and_13_out);
  and and_14 (and_14_out, or_10_out, Instruction[10]);
  and and_15 (and_15_out, D0, T4);
  and and_16 (and_16_out, D1, T4);
  and and_17 (and_17_out, D7, T4);
  and and_18 (and_18_out, D8, T4);
  and and_19 (and_19_out, D12, T4);
  and and_20 (and_20_out, D13, T4);
  and and_21 (and_21_out, D14, T4);
  and and_22 (and_22_out, or_7_out, or_8_out, T4);
  Decoder #(.select(2), .enable("false")) decoder_4 (
    .out0(RegSelGP_10_9[3]), .out1(RegSelGP_10_9[2]), .out2(RegSelGP_10_9[1]), .out3(RegSelGP_10_9[0]),
    .sel(Instruction[10:9]));
  assign OutputFunSelALU = and_15_out ? 4'b0101 : 4'bz;  // Controlled_Buffer controlled_buffer_7
  assign OutputFunSelALU = and_16_out ? 4'b0111 : 4'bz;  // Controlled_Buffer controlled_buffer_8
  assign OutputFunSelALU = and_17_out ? 4'b1010 : 4'bz;  // Controlled_Buffer controlled_buffer_9
  assign OutputFunSelALU = and_18_out ? 4'b1011 : 4'bz;  // Controlled_Buffer controlled_buffer_10
  assign OutputFunSelALU = and_19_out ? 4'b0010 : 4'bz;  // Controlled_Buffer controlled_buffer_11
  assign OutputFunSelALU = and_20_out ? 4'b0001 : 4'bz;  // Controlled_Buffer controlled_buffer_12
  assign OutputFunSelALU = and_21_out ? 4'b0000 : 4'bz;  // Controlled_Buffer controlled_buffer_13
  assign OutputFunSelALU = and_22_out ? 4'b0100 : 4'bz;  // Controlled_Buffer controlled_buffer_14
  Decoder #(.select(4), .enable("false")) decoder_5 (
    .out0(D0), .out1(D1), .out2(D2), .out3(D3), .out4(D4), .out5(D5), .out6(D6), .out7(D7), .out8(D8),
    .out9(D9), .out10(D10), .out11(D11), .out12(D12), .out13(D13), .out14(D14), .sel(Instruction[14:11]));  // open: out15
  not not_1 (not_1_out, T0);
  assign OutputRegSelASP = and_14_out ? RegSelASP_9_8 : 3'bz;  // Controlled_Buffer controlled_buffer_15
  or or_11 (OutputL_H, not_1_out, T2);
  or or_12 (OutputEnableIR, T0, T2);
  assign OutputFunSelIR = OutputEnableIR ? 2'b00 : 2'bz;  // Controlled_Buffer controlled_buffer_16
  or or_13 (or_13_out, D7, D8);
  and and_23 (and_23_out, or_13_out, ~Instruction[7]);  // AND_Gate
  and and_24 (and_24_out, D9, Instruction[8]);
  or or_14 (or_14_out, D0, D1, D7, D8, D12, D13, D14);
  assign OutputOutCsel = and_26_out ? Instruction[6:5] : 2'bz;  // Controlled_Buffer controlled_buffer_17
  assign OutputOutCsel = and_27_out ? 2'b00 : 2'bz;  // Controlled_Buffer controlled_buffer_18
  assign OutputOutCsel = or_19_out ? 2'b10 : 2'bz;  // Controlled_Buffer controlled_buffer_19
  assign OutputOutCsel = and_28_out ? Instruction[3:2] : 2'bz;  // Controlled_Buffer controlled_buffer_20
  or or_15 (or_15_out, D0, D1, D2, D3, and_23_out, D11, D12, D13, D14);
  or or_16 (or_16_out, D3, D2, or_14_out, D11);
  or or_17 (or_17_out, D0, D1, D13, D14);
  and and_25 (and_25_out, T4, or_17_out, Instruction[4]);
  assign OutputBSelALU = and_25_out ? 1'b1 : 1'bz;  // Controlled_Buffer controlled_buffer_21
  and and_26 (and_26_out, or_21_out, T4, Instruction[7]);
  or or_18 (or_18_out, and_33_out, D10);
  and and_27 (and_27_out, or_18_out, T4);
  or or_19 (or_19_out, T0, T2);
  and and_28 (and_28_out, and_38_out, T4, Instruction[4]);
  and and_29 (and_29_out, Instruction[8], D9, T4);
  and and_30 (and_30_out, ~Instruction[8], D9, T4);  // AND_Gate
  or or_20 (or_20_out, D2, D3);
  and and_31 (and_31_out, T4, Instruction[7], or_14_out);
  assign OutASelALU = and_31_out ? 1'b1 : 1'bz;  // Controlled_Buffer controlled_buffer_22
  and and_32 (and_32_out, T4, or_17_out, ~Instruction[4]);  // AND_Gate
  and and_33 (and_33_out, D9, ~Instruction[8]);  // AND_Gate
  assign OutputRegSelGP = and_29_out ? RegSelGP_10_9 : 4'bz;  // Controlled_Buffer controlled_buffer_23
  assign OutputRegSelGP = and_30_out ? RegSelGP_10_9 : 4'bz;  // Controlled_Buffer controlled_buffer_24
  and and_34 (and_34_out, ~Instruction[10], or_20_out, T5);  // AND_Gate
  assign OutputRegSelGP = and_34_out ? RegSelGP_9_8 : 4'bz;  // Controlled_Buffer controlled_buffer_25
  and and_35 (and_35_out, or_15_out, ~Instruction[10], T4);  // AND_Gate
  assign OutputRegSelGP = and_35_out ? RegSelGP_9_8 : 4'bz;  // Controlled_Buffer controlled_buffer_26
  and and_36 (and_36_out, D9, ~Instruction[8]);  // AND_Gate
  and and_37 (and_37_out, T4, ~Instruction[7], or_16_out);  // AND_Gate
  assign OutputOutASel = and_37_out ? Instruction[6:5] : 2'bz;  // Controlled_Buffer controlled_buffer_27
  assign OutASelALU = or_23_out ? 1'b0 : 1'bz;  // Controlled_Buffer controlled_buffer_28
  assign OutputOutBSel = and_32_out ? Instruction[3:2] : 2'bz;  // Controlled_Buffer controlled_buffer_29
  assign OutputBSelALU = and_32_out ? 1'b0 : 1'bz;  // Controlled_Buffer controlled_buffer_30
  or or_21 (or_21_out, D0, D1, D2, D7, D8, D11, D12, D13, D14, D3);
  or or_22 (or_22_out, D0, D1);
  and and_38 (and_38_out, or_22_out, ~Instruction[7]);  // AND_Gate
  assign OutputOutASel = and_39_out ? Instruction[10:9] : 2'bz;  // Controlled_Buffer controlled_buffer_31
  or or_23 (or_23_out, and_37_out, and_39_out);
  or or_24 (or_24_out, and_36_out, D14, D13, D12, D11, D10, and_24_out, D8, D7, D6, D5, D4, D1, D0);
  and and_39 (and_39_out, D10, T4);
  and and_40 (and_40_out, or_24_out, T4);
  and and_41 (and_41_out, D5, Z);
  and and_42 (and_42_out, D6, ~Z);  // AND_Gate
  or or_25 (or_25_out, D2, D3, D11);
  or or_26 (or_26_out, D0, D1, D2, D3, D7, D8, D11, D12, D13, D14);
  or or_27 (or_27_out, D3, D2);
  and and_43 (and_43_out, or_25_out, ~Instruction[7]);  // AND_Gate
  and and_44 (and_44_out, or_27_out, T5);
  and and_45 (and_45_out, Instruction[7], Instruction[10], or_28_out, T4);
  or or_28 (or_28_out, D3, D2, D11);
  or or_29 (or_29_out, D4, and_41_out, and_42_out, D10);
  and and_46 (and_46_out, or_29_out, T4);
  or or_30 (or_30_out, D0, D1, and_43_out, D7, D8, D12, D13, D14);
  and and_47 (and_47_out, or_26_out, ~Instruction[10], T4);  // AND_Gate
  and and_48 (and_48_out, Instruction[8], D9, T4);
  and and_49 (and_49_out, ~Instruction[8], D9, T4);  // AND_Gate
  or or_31 (SC, and_44_out, and_40_out);
  or or_32 (or_32_out, D0, D1, D2, D3, D7, D8, D11, D12, D13, D14);
  and and_50 (and_50_out, Instruction[10], T4, or_32_out);
  or or_33 (or_33_out, D0, D1);
  or or_34 (or_34_out, D13, D14);
  assign OutputSelASP = and_45_out ? 2'b00 : 2'bz;  // Controlled_Buffer controlled_buffer_32
  assign OutputSelASP = and_46_out ? 2'b01 : 2'bz;  // Controlled_Buffer controlled_buffer_33
  assign OutputSelASP = or_30_out ? 2'b11 : 2'bz;  // Controlled_Buffer controlled_buffer_34
  and and_51 (and_51_out, D2, Instruction[10], D5);
  and and_52 (and_52_out, D3, Instruction[10], T5);
  and and_53 (and_53_out, or_33_out, Instruction[7], Instruction[4], T4);
  or or_35 (or_35_out, and_53_out, and_54_out);
  and and_54 (and_54_out, Instruction[4], T4, or_34_out);
  and and_55 (and_55_out, ~Instruction[10], D2, T5);  // AND_Gate
  and and_56 (and_56_out, ~Instruction[10], D3, T5);  // AND_Gate
  or or_36 (or_36_out, and_47_out, and_48_out, and_49_out);
  or or_37 (or_37_out, D4, D10, and_59_out, and_58_out);
  and and_57 (and_57_out, T4, or_37_out);
  or or_38 (or_38_out, and_57_out, and_50_out);
  or or_39 (or_39_out, and_52_out, T1, T3);
  assign OutputOutDSel = or_35_out ? Instruction[3:2] : 2'bz;  // Controlled_Buffer controlled_buffer_35
  assign OutputFunSelGP = and_55_out ? 2'b01 : 2'bz;  // Controlled_Buffer controlled_buffer_36
  assign OutputFunSelGP = and_56_out ? 2'b10 : 2'bz;  // Controlled_Buffer controlled_buffer_37
  assign OutputFunSelGP = or_36_out ? 2'b00 : 2'bz;  // Controlled_Buffer controlled_buffer_38
  and and_58 (and_58_out, ~Z, D6);  // AND_Gate
  and and_59 (and_59_out, D5, Z);
  assign OutputFunSelASP = or_38_out ? 2'b00 : 2'bz;  // Controlled_Buffer controlled_buffer_39
  assign OutputFunSelASP = and_51_out ? 2'b01 : 2'bz;  // Controlled_Buffer controlled_buffer_40
  assign OutputFunSelASP = or_39_out ? 2'b10 : 2'bz;  // Controlled_Buffer controlled_buffer_41

  // Other names for the same wires on the sheet: ASelALU = OutASelALU; BSelALU = OutputBSelALU;
  //   EnableIR = OutputEnableIR; FunSelALU[3:0] = OutputFunSelALU; FunSelASP[1:0] = OutputFunSelASP;
  //   FunSelGP[1:0] = OutputFunSelGP; FunSelIR[1:0] = OutputFunSelIR; Address[7:0] = Instruction[7:0];
  //   IR_3_2[1:0] = Instruction[3:2]; SrcReg2[2:0] = Instruction[4:2]; IR_4 = Instruction[4];
  //   IR_6_5[1:0] = Instruction[6:5]; SrcReg1[2:0] = Instruction[7:5]; IR_7 = Instruction[7];
  //   AddressingMode = Instruction[8]; DestReg[2:0] = Instruction[10:8]; IR_8 = Instruction[8];
  //   IR_9_8[1:0] = Instruction[9:8]; RegSel[1:0] = Instruction[10:9]; IR_10 = Instruction[10];
  //   Opcode[3:0] = Instruction[14:11]; L_H_prime = OutputL_H; OutASel[1:0] = OutputOutASel;
  //   OutBSel[1:0] = OutputOutBSel; OutCSel[1:0] = OutputOutCsel; OutDSel[1:0] = OutputOutDSel; Read = MEMRead;
  //   RegSelASP[2:0] = OutputRegSelASP; RegSelGP[3:0] = OutputRegSelGP; SelASP[1:0] = OutputSelASP;
  //   SelGP[1:0] = OutputSelGP; Write = MEMWrite

  // Notes on the sheet:
  //   SelGP
  //   READ
  //   IR
  //   RegSelASP
  //   WRITE
  //   FunSelALU
  //   GP
  //   ALU
  //   ASP
  //   FunSelIR
  //   OutXSel
  //   L/H'
  //   Enable
  //   ASelALU
  //   OutBSel
  //   OutCSel
  //   RegSelGP
  //   OutASel
  //   BSelALU
  //   SC
  //   FunSelASP
  //   OutDSel
  //   SelASP
  //   FunSelGP
endmodule
